# Fritzing sketch Diagram v3 (saved by Fritzing 0.9.3b)
perfboards: 1

parts:
  Part1 = EasyDriver_v44
  M1 = Stepper Motor - Bipolar
  Part2 = EasyDriver_v44
  M2 = Stepper Motor - Bipolar
  S1 = Pushbutton [package="[THT]"]
  Part3 = Arduino Uno (Rev3) - ICSP
  R1 = Resistor [tolerance=±5% resistance=1k package="0603 [SMD]"]
  VCC2 = Battery block 9V [part_number="Power Supply"]

nets (from the breadboard view):
  GND: Part1.GND, Part2.GND, Part3.GND, R1.Pin_0, VCC2.-
  N1: Part1.V+, Part2.V+, VCC2.+
  N2: Part1.STEP, Part3.ICSP_MOSI, Part3.D11_PWM/MOSI
  N3: Part1.DIR, Part3.D12/MISO
  N4: Part1.OUT2A, M1.A
  N5: Part1.OUT2B, M1.C
  N6: Part1.OUT1A, M1.B
  N7: Part1.OUT1B, M1.D
  N8: Part2.STEP, Part3.D2
  N9: Part2.DIR, Part3.D7
  N10: Part2.OUT2A, M2.A
  N11: Part2.OUT2B, M2.C
  N12: Part2.OUT1A, M2.B
  N13: Part2.OUT1B, M2.D
  N14: S1.Pin_1, S1.Pin_2, Part3.3V3
  N15: S1.Pin_3, S1.Pin_4, Part3.D13/SCK, R1.Pin_1

notes:
  Red - Positive
  Black - Negative
  Green - IO
  Purple/Orange - Overside connections
  Blue - Underside connections
  Undo purple GND wire and replace with male-to-male jumper
  All orange wires should be female to male
  Add resistor
  Purple wires should be male-to-male
  Blue is connections on underside through pads
